# Fritzing sketch default_teensy3.6_sketch (saved by Fritzing 0.9.3b)
circuit board: 8.46667cm x 5.64444cm
breadboards: 1

parts:
  JP1 = M16 [package=1x16_machine-pin-header_lock.004]
  JP2 = M16 [package=1x16_machine-pin-header_lock.004]
  JP3 = M16 [package=1x16_machine-pin-header_lock.004]
  JP4 = M16 [package=1x16_machine-pin-header_lock.004]
  Teensy1 = Teensy 3.6 (Basic)

nets:
  N1: JP1.1, Teensy1.Vin
  N2: JP1.2, Teensy1.AGND
  N3: JP1.3, JP2.15, Teensy1.3V3, Teensy1.3V3_1
  N4: JP1.4, Teensy1.A9/D23
  N5: JP1.5, Teensy1.A8/D22
  N6: JP1.6, Teensy1.A7/D21
  N7: JP1.7, Teensy1.A6/D20
  N8: JP1.8, Teensy1.A5/D19
  N9: JP1.9, Teensy1.A4/D18
  N10: JP1.10, Teensy1.A3/D17
  N11: JP1.11, Teensy1.A2/D16
  N12: JP1.12, Teensy1.A1/D15
  N13: JP1.13, Teensy1.A0/D14
  N14: JP1.14, Teensy1.D13
  GND: JP1.15, JP2.1, Teensy1.GND, Teensy1.GND1
  N15: JP1.16, Teensy1.A22/DAC1
  N16: JP2.2, Teensy1.D0
  N17: JP2.3, Teensy1.D1
  N18: JP2.4, Teensy1.D2
  N19: JP2.5, Teensy1.D3
  N20: JP2.6, Teensy1.D4
  N21: JP2.7, Teensy1.D5
  N22: JP2.8, Teensy1.D6
  N23: JP2.9, Teensy1.D7
  N24: JP2.10, Teensy1.D8
  N25: JP2.11, Teensy1.D9
  N26: JP2.12, Teensy1.D10
  N27: JP2.13, Teensy1.D11
  N28: JP2.14, Teensy1.D12
  N29: JP2.16, Teensy1.D24
  N30: JP3.1, Teensy1.A21/DAC0
  N31: JP3.2, Teensy1.D39
  N32: JP3.3, Teensy1.D38
  N33: JP3.4, Teensy1.D37
  N34: JP3.5, Teensy1.D36
  N35: JP3.6, Teensy1.D35
  N36: JP3.7, Teensy1.D34
  N37: JP3.8, Teensy1.D33
  N38: JP4.1, Teensy1.D25
  N39: JP4.2, Teensy1.D26
  N40: JP4.3, Teensy1.D27
  N41: JP4.4, Teensy1.D28
  N42: JP4.5, Teensy1.D29
  N43: JP4.6, Teensy1.D30
  N44: JP4.7, Teensy1.D31
  N45: JP4.8, Teensy1.D32

custom parts:
  Teensy 3.6 (Basic): The Teensy is a complete USB-based microcontoller development system, in a very small footprint, capable of implementing many types of projects. All programming is done via the USB port. No special programmer is needed, only a standard micro-USB cable and a PC or Macintosh with a USB port.
